# Fritzing sketch Posha_submission_schematic (saved by Fritzing 1.0.6)

parts:
  Part1 = Arduino Uno (Rev3) - ICSP
  J1 = Basic Servo
  M1 = DC Motor [voltage_(max)=6V voltage_(min)=3V]
  Adafruit_AS5600_Magnetic_Angle_Sensor1 = Adafruit AS5600 Magnetic Angle Sensor [mn=Adafruit mpn=#6357 part_number=#6357]
  A1 = drv-1012
  INA1 = INA219 DC Current Sensor Breakout
  Part2 = HX711 Weighing Sensor Module
  Part3 = Current Sensor 5A
  Part4 = Adafruit ADS1115 16Bit I2C ADC [part_number="Adafruit #1085"]
  Load_Cell1 = Load Cell - Red/white/black/green
  Load_Cell2 = Load Cell - Red/white/black/green
  A2 = Hanmatek HM305

nets:
  N1: Part1.A4/SDA, Adafruit_AS5600_Magnetic_Angle_Sensor1.SDA, INA1.SDA, Part4.SDA
  N2: Part1.A5/SCL, Adafruit_AS5600_Magnetic_Angle_Sensor1.SCL, INA1.SCL, Part4.SCL
  N3: Part1.D8, A1.Pin_3
  N4: Part1.D9_PWM, J1.pulse
  N5: Part1.D10_PWM/SS, A1.Pin_8
  N6: Part1.D11_PWM/MOSI, A1.Pin_4
  N7: Part1.D2, Part2.CK/TX
  N8: Part1.D3_PWM, Part2.DO/RX
  N9: Part1.D7, A1.Pin_7
  VCC: Part1.5V, Adafruit_AS5600_Magnetic_Angle_Sensor1.VCC, INA1.VCC, Part2.VCC, Part3.VCC, Part4.VDD
  GND: Part1.GND, J1.gnd, Adafruit_AS5600_Magnetic_Angle_Sensor1.GND, A1.Pin_1, INA1.GND, INA1.Vin-, Part2.GND, Part3.GND, Part4.ADDR, Part4.GND
  N10: Part1.VIN, A1.Pin_5
  N11: J1.vcc, INA1.Vin+
  N12: M1.pin_1, Part3.1
  N13: M1.pin_2, A1.Pin_9
  N14: A1.Pin_10, Part3.2, Part3.OUT, Part4.AIN1
  N15: A1.Pin_11, A2.Pin_3
  N16: A1.Pin_12, A2.Pin_4
  N17: Part2.E+, Load_Cell1.wire1, Load_Cell2.wire1
  N18: Part2.E-, Load_Cell1.wire3, Load_Cell2.wire3
  N19: Part2.A+, Load_Cell1.wire2
  N20: Part2.A-, Load_Cell1.wire4
  N21: Part2.B+, Load_Cell2.wire2
  N22: Part2.B-, Load_Cell2.wire4

custom parts:
  drv-1012: .The BTS7960 is a fully integrated high current H bridge module for motor drive applications.
  INA219 DC Current Sensor Breakout: INA DC Current Sensor Breakout
  Adafruit ADS1115 16Bit I2C ADC: For microcontrollers without an analog-to-digital converter or when you want a higher-precision ADC, the ADS1115 provides 16-bit precision at 860 samples/second over I2C. The chip can be configured as 4 single-ended input channels, or two differential channels. As a nice bonus, it even includes a programmable gain amplifier, up to x16, to help boost up smaller single/differential signals to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
  Load Cell - Red/white/black/green: A rectangle load cell/weighting pressure Sensor with four wires - Red, white, black, green. Normally corresponding with E+, E-, A+, A- respectively.
  Hanmatek HM305: DC Power Supply 30V5A HM305.
